# Fritzing sketch bh1750 (saved by Fritzing 0.9.3b)

parts:
  Part4 = IoT WiFi Uno
  Part5 = BH1750

nets:
  5V: Part4.5V, Part5.VCC
  GND: Part4.GND, Part5.GND
  N1: Part4.GPIO04, Part5.SDA
  N2: Part4.GPIO05, Part5.SCL

custom parts:
  IoT WiFi Uno: ESP8266 WiFi Uno board
  BH1750: Light Sensor
