# Fritzing sketch chuyen_dong (saved by Fritzing 0.9.3b)

parts:
  Part1 = IoT WiFi Uno
  M1 = Dagu DGServo 9g (End View) [part_number=RS001B]  # not connected
  SERVO1 = Tower Pro SG90 servo [part_number=101246]

nets:
  N1: Part1.GPIO2, SERVO1.Signal
  5V: Part1.5V, SERVO1.+5V
  GND: Part1.GND, SERVO1.GND

custom parts:
  IoT WiFi Uno: ESP8266 WiFi Uno board
  Tower Pro SG90 servo: Original file by John De Cristofaro http://www.adafruit.com/products/1449 Adafruit Feedback Servo (Small) Edited by: e-radionica.com 28/9/2015
