# Fritzing sketch ds18b20_1 (saved by Fritzing 0.9.3b)
breadboards: 1

parts:
  Part3 = IoT WiFi Uno
  DS1 = DS18B20 1-Wire Temperature Sensor [part_number=DS18B20]

nets:
  N1: Part3.GPIO2, DS1.DQ
  5V: Part3.5V, DS1.VDD
  GND: Part3.GND, DS1.GND

custom parts:
  IoT WiFi Uno: ESP8266 WiFi Uno board
