# Fritzing sketch exam2 (saved by Fritzing 0.9.3b)
breadboards: 1

parts:
  Part2 = IoT WiFi Uno
  HC-SR502 = HC-SR501 Body Sensor Module
  Part3 = BH1750
  LED1 = LEDs [package=led10mm]
  DHT2 = DHT11 Humitidy and Temperature Sensor (3 pins)
  SERVO1 = Tower Pro SG90 servo [part_number=101246]

nets:
  N1: Part2.GPIO0, SERVO1.Signal
  N2: Part2.GPIO2, Part2.RST, HC-SR502.OUT
  N3: Part2.GPIO12, LED1.C
  N4: Part2.GPIO4, DHT2.VDD
  VCC: Part2.5V, HC-SR502.VCC, Part3.VCC, DHT2.DATA, SERVO1.+5V
  GND: Part2.GND, HC-SR502.GND, Part3.GND, LED1.A, DHT2.GND, SERVO1.GND
  N5: Part2.GPIO04, Part3.SDA
  N6: Part2.GPIO05, Part3.SCL

custom parts:
  IoT WiFi Uno: ESP8266 WiFi Uno board
  HC-SR501 Body Sensor Module: Pyroelectric Infrared PIR Motion Sensor Detector Module
  BH1750: Light Sensor
  DHT11 Humitidy and Temperature Sensor (3 pins): DHT11 Humidity and Temperature Sensor (3 pins) from the design created by John De Cristofaro for Adafruit Industries.
  Tower Pro SG90 servo: Original file by John De Cristofaro http://www.adafruit.com/products/1449 Adafruit Feedback Servo (Small) Edited by: e-radionica.com 28/9/2015
