# Fritzing sketch exam3 (saved by Fritzing 0.9.3b)
breadboards: 1

parts:
  Part4 = IoT WiFi Uno
  HC-SR503 = HC-SR501 Body Sensor Module
  Part5 = BH1750
  LED2 = LEDs [package=led10mm]
  SERVO2 = Tower Pro SG90 servo [part_number=101246]
  DS1 = DS18B20 1-Wire Temperature Sensor [part_number=DS18B20]

nets:
  N1: Part4.GPIO0, SERVO2.Signal
  N2: Part4.GPIO2, Part4.RST, DS1.DQ
  N3: Part4.GPIO10, Part4.SCL, HC-SR503.OUT
  N4: Part4.GPIO12, LED2.C
  VCC: Part4.5V, HC-SR503.VCC, Part5.VCC, SERVO2.+5V, DS1.VDD
  GND: Part4.GND, HC-SR503.GND, Part5.GND, LED2.A, SERVO2.GND, DS1.GND
  N5: Part4.GPIO04, Part5.SDA
  N6: Part4.GPIO05, Part5.SCL

custom parts:
  IoT WiFi Uno: ESP8266 WiFi Uno board
  HC-SR501 Body Sensor Module: Pyroelectric Infrared PIR Motion Sensor Detector Module
  BH1750: Light Sensor
  Tower Pro SG90 servo: Original file by John De Cristofaro http://www.adafruit.com/products/1449 Adafruit Feedback Servo (Small) Edited by: e-radionica.com 28/9/2015
