# Fritzing sketch mua (saved by Fritzing 0.9.3b)

parts:
  Part2 = IoT WiFi Uno
  YL-83_-_Detection_Board1 = YL-83 Rain Sensor - Detection Board
  YL-83_-_Control_Board1 = YL-83 Rain Sensor - Control Board

nets:
  3V3: Part2.CS0, Part2.3V3, YL-83_-_Control_Board1.VCC
  GND: Part2.GND, YL-83_-_Control_Board1.GND
  N1: Part2.ADC, YL-83_-_Control_Board1.AO
  N2: YL-83_-_Detection_Board1.POS, YL-83_-_Control_Board1.NEG
  N3: YL-83_-_Detection_Board1.NEG, YL-83_-_Control_Board1.POS

custom parts:
  IoT WiFi Uno: ESP8266 WiFi Uno board
  YL-83 Rain Sensor - Detection Board: The YL-83 is a rain sensor that has more resistance when dry and less resistance when wet. The module runs at 5V.
  YL-83 Rain Sensor - Control Board: The YL-83 is a rain sensor that has more resistance when dry and less resistance when wet. The module runs at 5V.
